# Fritzing sketch tank (saved by Fritzing 0.6.5b)
breadboards: 1

parts:
  Arduino1 = Arduino
  IC1 = L293D [package=THT]  # not connected
  IC2 = L293D [package=THT]
  VCC1 = Battery block 9V
  U1 = mystery part, 3 pins [chip_label=IR spacing=300mil]
  M1 = Stepper Motor - Bipolar
  R1 = Resistor [tolerance=±5% resistance=220 package=THT]
  R2 = Resistor [tolerance=±5% resistance=220 package=THT]
  R3 = Resistor [tolerance=±5% resistance=220 package=THT]
  R4 = Resistor [tolerance=±5% resistance=220 package=THT]
  LED1 = LED - 3mm [color="Orange (605nm)" package="3 mm [THT]"]
  LED2 = LED - 3mm [color="Orange (605nm)" package="3 mm [THT]"]
  LED3 = LED - 3mm [color="Orange (605nm)" package="3 mm [THT]"]
  LED4 = LED - 3mm [color="Orange (605nm)" package="3 mm [THT]"]

nets:
  N1: Arduino1.D9, IC2.In_1
  N2: Arduino1.D8, IC2.In_2
  N3: Arduino1.D7, IC2.In_3
  N4: Arduino1.D6, IC2.In_4
  N5: Arduino1.D3, U1.pin2
  N6: Arduino1.GND, LED1.cathode, LED2.cathode, LED3.cathode, LED4.cathode
  N7: IC2.Enable_1, IC2.Enable_2, IC2.+V, U1.pin3
  N8: IC2.Out_1_(_Controlled_by_Enable_1_), M1.C, R4.Pin_1
  N9: IC2.0V, VCC1.-, U1.pin1
  N10: IC2.Out_2_(_Controlled_by_Enable_1_), M1.A, R1.Pin_1
  N11: IC2.+Vmotor, VCC1.+
  N12: IC2.Out_3_(_Controlled_by_Enable_2_), M1.D, R3.Pin_1
  N13: IC2.Out_4_(_Controlled_by_Enable_2_), M1.B, R2.Pin_1
  N14: R1.Pin_0, LED4.anode
  N15: R2.Pin_0, LED2.anode
  N16: R3.Pin_0, LED1.anode
  N17: R4.Pin_0, LED3.anode
